# Fritzing sketch Mini Cube Breadboard (saved by Fritzing 0.9.3b)
perfboards: 1

parts:
  RCWL-0516_Microwave_Radar_Motion_Sensor1 = RCWL-0516 Microwave Radar Motion Sensor Module
  Nano1 = Arduino Nano v2.3
  Part1 = ws2812b [package="smd 2812b"]
  R21 = Resistor [tolerance=±5% resistance=330 package="2010 [SMD]"]
  Part2 = Adafruit MAX9814 Electret Microphone Amplifier [part_number="Adafruit #1713"]

nets:
  GND: RCWL-0516_Microwave_Radar_Motion_Sensor1.GND, Part2.GND
  VDD: RCWL-0516_Microwave_Radar_Motion_Sensor1.VIN, Part1.VDD, Part2.VDD
  N1: Nano1.D2, R21.Pin_1
  N2: Nano1.A6, Part2.OUTPUT
  N3: Part1.DIN, R21.Pin_0

custom parts:
  RCWL-0516 Microwave Radar Motion Sensor Module: The RCWL-0516 is a microwave radar motion sensor module. Input voltage is 4V to 28V. The 3V3 pin is a power output.
  Adafruit MAX9814 Electret Microphone Amplifier: Add an ear to your project with this well-designed electret microphone amplifier with AGC. This fully assembled and tested board comes with a 20-20KHz electret microphone soldered on. For the amplification, we use the Maxim MAX9814, a specialty chip that is designed for amplifying electret microphones in situations where the loudness of the audio isn't predictable. This fancy microphone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
